# Fritzing sketch Ultrasonic_Instrument (saved by Fritzing 0.7.12b)
breadboards: 1
perfboards: 1

parts:
  Arduino2 = Arduino
  U2 = 74HC595 [package="DIP16 [THT]"]
  U3 = 74HC595 [package="DIP16 [THT]"]
  U4 = atmega328 [package=dip]
  LED1 = LED - 5mm [color="Blue (430nm)" package="5 mm [THT]"]
  LED7 = LED - 5mm [color="White (8000K)" package="5 mm [THT]"]
  LED8 = LED - 5mm [color="White (8000K)" package="5 mm [THT]"]
  LED9 = LED - 5mm [color="Blue (430nm)" package="5 mm [THT]"]
  LED10 = LED - 5mm [color="White (8000K)" package="5 mm [THT]"]
  LED11 = LED - 5mm [color="Blue (430nm)" package="5 mm [THT]"]
  LED12 = LED - 5mm [color="White (8000K)" package="5 mm [THT]"]
  LED13 = LED - 5mm [color="Blue (430nm)" package="5 mm [THT]"]
  LED14 = LED - 5mm [color="Blue (430nm)" package="5 mm [THT]"]
  LED15 = LED - 5mm [color="White (8000K)" package="5 mm [THT]"]
  LED16 = LED - 5mm [color="Blue (430nm)" package="5 mm [THT]"]
  LED17 = LED - 5mm [color="White (8000K)" package="5 mm [THT]"]
  LED18 = LED - 5mm [color="Blue (430nm)" package="5 mm [THT]"]
  LED19 = LED - 5mm [color="White (8000K)" package="5 mm [THT]"]
  LED20 = LED - 5mm [color="Blue (430nm)" package="5 mm [THT]"]
  LED21 = LED - 5mm [color="White (8000K)" package="5 mm [THT]"]
  R1 = Resistor [tolerance=±5% resistance=220 package=THT]
  VCC1 = 4 x AAA Battery Mount  # not connected
  U5 = Voltage Regulator - 5V [package="TO220 [THT]"]  # not connected
  C1 = Electrolytic Capacitor [capacitance=10µF package="100 mil [THT, electrolytic]"]
  C2 = Electrolytic Capacitor [capacitance=10µF package="100 mil [THT, electrolytic]"]
  SPKR1 = Loudspeaker  # not connected
  S1 = Pushbutton [package="[THT]"]
  S2 = Pushbutton [package="[THT]"]
  S3 = Pushbutton [package="[THT]"]
  S4 = Pushbutton [package="[THT]"]
  R2 = Resistor [tolerance=±5% resistance=220 package=THT]
  R3 = Resistor [tolerance=±5% resistance=220 package=THT]
  Part1 = SRF05 Ultrasonic Rangefinder
  LED22 = LED - 5mm [color="Red (633nm)" package="5 mm [THT]"]

nets:
  N1: Arduino2.D12, U2.SH_CP
  N2: Arduino2.D11, U2.DS
  N3: Arduino2.D8, U2.ST_CP
  N4: U2.Q1, LED7.anode
  N5: U2.Q2, LED9.anode
  N6: U2.Q3, LED8.anode
  N7: U2.Q4, LED11.anode
  N8: U2.Q5, LED10.anode
  N9: U2.Q6, LED13.anode
  N10: U2.Q7, LED12.anode
  N11: U2.MR, U2.VCC
  N12: U2.Q0, LED1.anode
  N13: U3.Q1, LED15.anode
  N14: U3.Q2, LED16.anode
  N15: U3.Q3, LED17.anode
  N16: U3.Q4, LED18.anode
  N17: U3.Q5, LED19.anode
  N18: U3.Q6, LED20.anode
  N19: U3.Q7, LED21.anode
  GND: U3.GND, U3.ST_CP, R1.Pin_1, Part1.GND
  N20: U3.SH_CP, U4.D12
  N21: U3.DS, U4.D11_(PWM)
  VCC: U3.VCC, U4.VCC, U4.AVCC, C1.+, R2.Pin_1, R3.Pin_1, Part1.VCC
  N22: U4.D2, Part1.Echo
  N23: U4.D3_(PWM), Part1.Trig
  N24: U4.D4, S1.Pin_1, S1.Pin_2, R2.Pin_0
  N25: U4.D7, S2.Pin_1, S2.Pin_2, R3.Pin_0
  N26: LED14.cathode, LED22.cathode
  N27: LED19.cathode, LED20.cathode, LED21.cathode
  N28: C1.-, C2.-
  N29: S1.Pin_3, S1.Pin_4, S2.Pin_3, S2.Pin_4
  N30: S3.Pin_1, S3.Pin_2
  N31: S3.Pin_3, S3.Pin_4
  N32: S4.Pin_1, S4.Pin_2
  N33: S4.Pin_3, S4.Pin_4
